// Logisim project elec2.circ as structural Verilog: 4 circuits, main circuit mux4-1
// MUX
module mux4_1 (
  input  A0,
  input  A1,
  input  D0,
  input  D1,
  input  D2,
  input  D3,
  output Y
);

  wire not_1_out, not_2_out, \и_2_out , \и_3_out , \и_4_out , \и_out ;

  not not_1 (not_1_out, A1);
  not not_2 (not_2_out, A0);
  and \u_и  (\и_out , not_2_out, not_1_out, D0);
  and \u_и_2  (\и_2_out , not_1_out, A0, D1);
  and \u_и_3  (\и_3_out , not_2_out, D2, A1);
  and \u_и_4  (\и_4_out , A0, D3, A1);
  or \u_или  (Y, \и_out , \и_2_out , \и_3_out , \и_4_out );
endmodule

module mux16_1 (
  input  D0,
  input  D1,
  input  D2,
  input  D3,
  input  D4,
  input  D5,
  input  D6,
  input  D7,
  input  D8,
  input  D9,
  input  D10,
  input  D11,
  input  D12,
  input  D13,
  input  D14,
  input  D15,
  input  A0,
  input  A1,
  input  A2,
  input  A3,
  output out_21
);

  wire mux4_1_1_y, mux4_1_2_y, mux4_1_3_y, mux4_1_4_y;

  mux4_1 mux4_1_1 (.A0(A0), .A1(A1), .D0(D0), .D1(D1), .D2(D2), .D3(D3), .Y(mux4_1_1_y));
  mux4_1 mux4_1_2 (.A0(A0), .A1(A1), .D0(D4), .D1(D5), .D2(D6), .D3(D7), .Y(mux4_1_2_y));
  mux4_1 mux4_1_3 (.A0(A0), .A1(A1), .D0(D8), .D1(D9), .D2(D10), .D3(D11), .Y(mux4_1_3_y));
  mux4_1 mux4_1_4 (.A0(A0), .A1(A1), .D0(D12), .D1(D13), .D2(D14), .D3(D15), .Y(mux4_1_4_y));
  mux4_1 mux4_1_5 (.A0(A2), .A1(A3), .D0(mux4_1_1_y), .D1(mux4_1_2_y), .D2(mux4_1_3_y), .D3(mux4_1_4_y), .Y(out_21));
endmodule

module DEMUL (
  input  D,
  input  A0,
  input  A1,
  output Y0,
  output Y1,
  output Y2,
  output Y3
);

  wire mux4_1_1_p5, mux4_1_1_p6, mux4_1_1_p7, mux4_1_1_p8, mux4_1_1_p9, mux4_1_1_p10, mux4_1_1_p11,
       nand_1_out, nand_2_out, nand_3_out, nand_4_out, nand_5_out, nand_6_out, nand_7_out, nand_8_out;

  nand nand_1 (nand_1_out, A0, A0);
  nand nand_2 (nand_2_out, A1, A1);
  nand nand_3 (nand_3_out, A1, A1);
  nand nand_4 (nand_4_out, A0, A0);
  nand nand_5 (nand_5_out, D, A0, A1);
  nand nand_6 (nand_6_out, D, nand_1_out, nand_2_out);
  nand nand_7 (nand_7_out, D, nand_3_out, A0);
  nand nand_8 (nand_8_out, D, A1, nand_4_out);
  nand nand_9 (Y3, nand_5_out, nand_5_out);
  _7_Segment_Display u_7_segment_display_1 (
    .g(mux4_1_1_p11), .f(mux4_1_1_p10), .a(mux4_1_1_p5), .b(mux4_1_1_p6), .e(mux4_1_1_p9), .d(mux4_1_1_p8),
    .c(mux4_1_1_p7));  // open: dp
  nand nand_10 (Y0, nand_6_out, nand_6_out);
  nand nand_11 (Y1, nand_7_out, nand_7_out);
  nand nand_12 (Y2, nand_8_out, nand_8_out);
  // mux4_1 mux4_1_1: pin names not known; wires that end beside it: Y3, Y2, Y1, Y0, mux4_1_1_p5, mux4_1_1_p6, mux4_1_1_p7, mux4_1_1_p8, mux4_1_1_p9, mux4_1_1_p10, mux4_1_1_p11
endmodule

module deshif (
  input  Y3,
  input  Y2,
  input  Y1,
  input  Y0,
  output a,
  output b,
  output c,
  output d,
  output e,
  output f,
  output g
);

  wire nand_1_out, nand_2_out, nand_3_out, nand_4_out, nand_5_out, nand_6_out, nand_7_out, nand_8_out,
       nand_9_out, nand_10_out, nand_11_out, nand_12_out, nand_13_out, nand_14_out, nand_15_out, nand_16_out,
       nand_17_out, nand_18_out, nand_19_out, nand_20_out, nand_21_out, nand_22_out, nand_23_out,
       nand_24_out, nand_25_out, nand_26_out, nand_27_out, nand_28_out, nand_29_out, nand_30_out,
       nand_31_out, nand_32_out, nand_33_out, nand_34_out, nand_35_out, nand_36_out, nand_37_out,
       nand_38_out, nand_39_out, nand_40_out, nand_41_out, nand_42_out, nand_43_out, nand_44_out,
       nand_45_out, nand_46_out, nand_47_out, nand_48_out, nand_49_out, nand_50_out, nand_51_out,
       nand_52_out, nand_53_out, nand_54_out, nand_55_out, nand_56_out, nand_57_out, nand_58_out,
       nand_59_out, nand_60_out, nand_61_out, nand_62_out, nand_63_out, nand_64_out, nand_65_out,
       nand_66_out, nand_67_out, nand_68_out, nand_69_out, nand_70_out, nand_71_out, nand_72_out,
       nand_73_out, nand_74_out, nand_75_out, nand_76_out, nand_77_out, nand_78_out, nand_79_out,
       nand_80_out, nand_81_out, nand_82_out, nand_83_out, nand_84_out, nand_85_out, nand_86_out,
       nand_87_out, nand_88_out, nand_89_out, nand_90_out, nand_91_out, nand_92_out, nand_93_out,
       nand_94_out, nand_95_out, nand_96_out, nand_97_out, nand_98_out, nand_99_out, nand_100_out,
       nand_101_out, nand_102_out, nand_103_out, nand_104_out, nand_105_out, nand_106_out, nand_107_out,
       nand_108_out, nand_109_out, nand_110_out, nand_111_out, nand_112_out, nand_113_out, nand_114_out,
       nand_115_out, nand_116_out, nand_117_out, nand_118_out, nand_120_out, nand_121_out, nand_122_out,
       nand_123_out, nand_124_out, nand_125_out, nand_126_out, nand_128_out, nand_129_out, nand_130_out,
       nand_131_out, nand_132_out, nand_133_out, nand_134_out, nand_135_out, nand_136_out, nand_137_out,
       nand_138_out, nand_139_out, nand_140_out, nand_141_out, nand_142_out, nand_143_out, nand_146_out,
       nand_147_out, nand_150_out, nand_151_out;

  nand nand_1 (nand_1_out, Y3, Y3);
  nand nand_2 (nand_2_out, Y2, Y2);
  nand nand_3 (nand_3_out, Y3, Y3);
  nand nand_4 (nand_4_out, Y2, Y2);
  nand nand_5 (nand_5_out, Y3, Y3);
  nand nand_6 (nand_6_out, Y1, Y1);
  nand nand_7 (nand_7_out, Y3, Y3);
  nand nand_8 (nand_8_out, Y2, Y2);
  nand nand_9 (nand_9_out, Y1, Y1);
  nand nand_10 (nand_10_out, Y3, Y3);
  nand nand_11 (nand_11_out, Y3, Y3);
  nand nand_12 (nand_12_out, Y2, Y2);
  nand nand_13 (nand_13_out, Y3, Y3);
  nand nand_14 (nand_14_out, Y2, Y2);
  nand nand_15 (nand_15_out, Y2, Y2);
  nand nand_16 (nand_16_out, Y1, Y1);
  nand nand_17 (nand_17_out, Y3, Y3);
  nand nand_18 (nand_18_out, Y3, Y3);
  nand nand_19 (nand_19_out, Y1, Y1);
  nand nand_20 (nand_20_out, Y3, Y3);
  nand nand_21 (nand_21_out, Y3, Y3);
  nand nand_22 (nand_22_out, Y2, Y2);
  nand nand_23 (nand_23_out, Y3, Y3);
  nand nand_24 (nand_24_out, Y1, Y1);
  nand nand_25 (nand_25_out, Y3, Y3);
  nand nand_26 (nand_26_out, Y3, Y3);
  nand nand_27 (nand_27_out, Y2, Y2);
  nand nand_28 (nand_28_out, nand_1_out, nand_2_out);
  nand nand_29 (nand_29_out, nand_3_out, Y2);
  nand nand_30 (nand_30_out, Y3, nand_4_out);
  nand nand_31 (nand_31_out, nand_5_out, nand_6_out);
  nand nand_32 (nand_32_out, nand_7_out, Y1);
  nand nand_33 (nand_33_out, nand_8_out, nand_9_out);
  nand nand_34 (nand_34_out, nand_10_out, Y0);
  nand nand_35 (nand_35_out, nand_11_out, nand_12_out);
  nand nand_36 (nand_36_out, nand_13_out, nand_14_out);
  nand nand_37 (nand_37_out, nand_15_out, nand_16_out);
  nand nand_38 (nand_38_out, nand_17_out, Y1);
  nand nand_39 (nand_39_out, nand_18_out, nand_19_out);
  nand nand_40 (nand_40_out, nand_20_out, Y2);
  nand nand_41 (nand_41_out, nand_21_out, Y2);
  nand nand_42 (nand_42_out, Y3, nand_22_out);
  nand nand_43 (nand_43_out, nand_23_out, nand_24_out);
  nand nand_44 (nand_44_out, nand_25_out, Y2);
  nand nand_45 (nand_45_out, nand_26_out, Y2);
  nand nand_46 (nand_46_out, Y3, nand_27_out);
  nand nand_47 (nand_47_out, nand_28_out, nand_28_out);
  nand nand_48 (nand_48_out, Y0, Y0);
  nand nand_49 (nand_49_out, Y3, Y3);
  nand nand_50 (nand_50_out, nand_29_out, nand_29_out);
  nand nand_51 (nand_51_out, nand_30_out, nand_30_out);
  nand nand_52 (nand_52_out, Y1, Y1);
  nand nand_53 (nand_53_out, Y3, Y3);
  nand nand_54 (nand_54_out, Y2, Y2);
  nand nand_55 (nand_55_out, nand_31_out, nand_31_out);
  nand nand_56 (nand_56_out, Y0, Y0);
  nand nand_57 (nand_57_out, Y2, Y2);
  nand nand_58 (nand_58_out, Y1, Y1);
  nand nand_59 (nand_59_out, nand_32_out, nand_32_out);
  nand nand_60 (nand_60_out, nand_33_out, nand_34_out);
  nand nand_61 (nand_61_out, Y3, Y3);
  nand nand_62 (nand_62_out, nand_35_out, nand_35_out);
  nand nand_63 (nand_63_out, Y0, Y0);
  nand nand_64 (nand_64_out, nand_36_out, nand_36_out);
  nand nand_65 (nand_65_out, Y3, Y3);
  nand nand_66 (nand_66_out, Y3, Y3);
  nand nand_67 (nand_67_out, Y1, Y1);
  nand nand_68 (nand_68_out, Y2, Y2);
  nand nand_69 (nand_69_out, nand_37_out, nand_37_out);
  nand nand_70 (nand_70_out, Y0, Y0);
  nand nand_71 (nand_71_out, nand_38_out, nand_38_out);
  nand nand_72 (nand_72_out, Y0, Y0);
  nand nand_73 (nand_73_out, nand_39_out, nand_39_out);
  nand nand_74 (nand_74_out, Y0, Y0);
  nand nand_75 (nand_75_out, nand_40_out, nand_40_out);
  nand nand_76 (nand_76_out, Y1, Y1);
  nand nand_77 (nand_77_out, nand_41_out, nand_41_out);
  nand nand_78 (nand_78_out, Y0, Y0);
  nand nand_79 (nand_79_out, nand_42_out, nand_42_out);
  nand nand_80 (nand_80_out, Y1, Y1);
  nand nand_81 (nand_81_out, nand_43_out, nand_43_out);
  nand nand_82 (nand_82_out, Y0, Y0);
  nand nand_83 (nand_83_out, nand_44_out, nand_44_out);
  nand nand_84 (nand_84_out, Y1, Y1);
  nand nand_85 (nand_85_out, nand_45_out, nand_45_out);
  nand nand_86 (nand_86_out, Y0, Y0);
  nand nand_87 (nand_87_out, nand_46_out, nand_46_out);
  nand nand_88 (nand_88_out, Y1, Y1);
  nand nand_89 (nand_89_out, nand_47_out, nand_48_out);
  nand nand_90 (nand_90_out, nand_49_out, Y1);
  nand nand_91 (nand_91_out, nand_50_out, Y0);
  nand nand_92 (nand_92_out, nand_51_out, nand_52_out);
  nand nand_93 (nand_93_out, nand_53_out, nand_54_out);
  nand nand_94 (nand_94_out, nand_55_out, nand_56_out);
  nand nand_95 (nand_95_out, nand_57_out, nand_58_out);
  nand nand_96 (nand_96_out, nand_59_out, Y0);
  nand nand_97 (nand_97_out, nand_60_out, nand_60_out);
  nand nand_98 (nand_98_out, nand_61_out, Y2);
  nand nand_99 (nand_99_out, nand_62_out, nand_63_out);
  nand nand_100 (nand_100_out, nand_64_out, Y1);
  nand nand_101 (nand_101_out, nand_65_out, Y1);
  nand nand_102 (nand_102_out, nand_66_out, Y2);
  nand nand_103 (nand_103_out, nand_67_out, Y0);
  nand nand_104 (nand_104_out, Y3, nand_68_out);
  nand nand_105 (nand_105_out, nand_69_out, nand_70_out);
  nand nand_106 (nand_106_out, nand_71_out, nand_72_out);
  nand nand_107 (nand_107_out, nand_73_out, nand_74_out);
  nand nand_108 (nand_108_out, nand_75_out, nand_76_out);
  nand nand_109 (nand_109_out, nand_77_out, nand_78_out);
  nand nand_110 (nand_110_out, nand_79_out, nand_80_out);
  nand nand_111 (nand_111_out, nand_81_out, nand_82_out);
  nand nand_112 (nand_112_out, nand_83_out, nand_84_out);
  nand nand_113 (nand_113_out, nand_85_out, nand_86_out);
  nand nand_114 (nand_114_out, nand_87_out, nand_88_out);
  nand nand_115 (nand_115_out, nand_89_out, nand_90_out);
  nand nand_116 (nand_116_out, nand_91_out, nand_92_out);
  nand nand_117 (nand_117_out, nand_93_out, nand_94_out);
  nand nand_118 (nand_118_out, nand_95_out, nand_96_out);
  nand nand_119 (c, nand_97_out, nand_98_out);
  nand nand_120 (nand_120_out, nand_99_out, nand_100_out);
  nand nand_121 (nand_121_out, nand_101_out, nand_101_out);
  nand nand_122 (nand_122_out, Y0, Y0);
  nand nand_123 (nand_123_out, nand_102_out, nand_102_out);
  nand nand_124 (nand_124_out, nand_103_out, nand_103_out);
  nand nand_125 (nand_125_out, nand_104_out, nand_104_out);
  nand nand_126 (nand_126_out, Y1, Y1);
  nand nand_127 (e, nand_105_out, nand_106_out);
  nand nand_128 (nand_128_out, nand_107_out, nand_108_out);
  nand nand_129 (nand_129_out, nand_109_out, nand_110_out);
  nand nand_130 (nand_130_out, nand_111_out, nand_112_out);
  nand nand_131 (nand_131_out, nand_113_out, nand_114_out);
  nand nand_132 (nand_132_out, nand_115_out, nand_115_out);
  nand nand_133 (nand_133_out, nand_116_out, nand_116_out);
  nand nand_134 (nand_134_out, nand_117_out, nand_117_out);
  nand nand_135 (nand_135_out, nand_118_out, nand_118_out);
  nand nand_136 (nand_136_out, nand_120_out, nand_120_out);
  nand nand_137 (nand_137_out, nand_121_out, nand_122_out);
  nand nand_138 (nand_138_out, nand_123_out, nand_124_out);
  nand nand_139 (nand_139_out, nand_125_out, nand_126_out);
  nand nand_140 (nand_140_out, nand_128_out, nand_128_out);
  nand nand_141 (nand_141_out, nand_129_out, nand_129_out);
  nand nand_142 (nand_142_out, nand_130_out, nand_130_out);
  nand nand_143 (nand_143_out, nand_131_out, nand_131_out);
  nand nand_144 (a, nand_132_out, nand_133_out);
  nand nand_145 (b, nand_134_out, nand_135_out);
  nand nand_146 (nand_146_out, nand_136_out, nand_137_out);
  nand nand_147 (nand_147_out, nand_138_out, nand_139_out);
  nand nand_148 (f, nand_140_out, nand_141_out);
  nand nand_149 (g, nand_142_out, nand_143_out);
  nand nand_150 (nand_150_out, nand_146_out, nand_146_out);
  nand nand_151 (nand_151_out, nand_147_out, nand_147_out);
  nand nand_152 (d, nand_150_out, nand_151_out);
endmodule
